# Fritzing sketch ClaudioSchematics (saved by Fritzing 0.9.6b)
breadboards: 1

parts:
  Mod1 = Heltec WiFi LoRa 32 V2 [part_number=HTIT-WB32LA]
  RW = PHOTOTRANSISTOR REFLECTIVE OBJECT SENSOR [package=qrb1114-side]
  LW = PHOTOTRANSISTOR REFLECTIVE OBJECT SENSOR [package=qrb1114-side]
  RB = PHOTOTRANSISTOR REFLECTIVE OBJECT SENSOR [package=qrb1114-side]
  LWall = PHOTOTRANSISTOR REFLECTIVE OBJECT SENSOR [package=qrb1114-side]
  LDrop = PHOTOTRANSISTOR REFLECTIVE OBJECT SENSOR [package=qrb1114-side]
  FDrop = PHOTOTRANSISTOR REFLECTIVE OBJECT SENSOR [package=qrb1114-side]
  RDrop = PHOTOTRANSISTOR REFLECTIVE OBJECT SENSOR [package=qrb1114-side]
  IR1 = TSOP312.., 314.. [package=THT]
  IR2 = TSOP312.., 314.. [package=THT]
  R1 = Resistor [tolerance=±5% power=0.25 resistance=1000 package=THT]
  R2 = Resistor [tolerance=±5% power=0.25 resistance=1000 package=THT]
  R3 = Resistor [tolerance=±5% power=0.25 resistance=1000 package=THT]
  R4 = Resistor [tolerance=±5% power=0.25 resistance=1000 package=THT]
  R5 = Resistor [tolerance=±5% power=0.25 resistance=1000 package=THT]
  R6 = Resistor [tolerance=±5% power=0.25 resistance=1000 package=THT]
  R7 = Resistor [tolerance=±5% power=0.25 resistance=1000 package=THT]
  R8 = Resistor [tolerance=±5% power=0.25 resistance=1000 package=THT]
  Motores = Adafruit DRV8833 DC/Stepper Motor Driver [part_number="Adafruit #3297"]
  Turbina = Adafruit DRV8833 DC/Stepper Motor Driver [part_number="Adafruit #3297"]
  Part3 = InvenSense MPU6050
  M1 = RioRand LM2596
  Escovas = Adafruit DRV8833 DC/Stepper Motor Driver [part_number="Adafruit #3297"]
  LB = PHOTOTRANSISTOR REFLECTIVE OBJECT SENSOR [package=qrb1114-side]
  R12 = Resistor [tolerance=±5% power=0.25 resistance=1000 package=THT]
  R13 = Resistor [tolerance=±5% power=0.25 resistance=1000 package=THT]

nets (from the schematic view):
  N1: Mod1.pin_1, Part3.SDA
  N2: Mod1.pin_2, RW.C
  N3: Mod1.pin_3, LW.C
  N4: Mod1.pin_4, IR2.Data
  N5: Mod1.pin_10, Escovas.AIN2
  N6: Mod1.pin_11, Turbina.BIN1
  N7: Mod1.pin_12, Motores.AIN1
  N8: Mod1.pin_13, Motores.AIN2
  N9: Mod1.pin_14, Motores.BIN2
  N10: Mod1.pin_15, Motores.BIN1
  N11: Mod1.pin_16, Mod1.pin_17, R1.Pin_0, R2.Pin_0, R3.Pin_0, R4.Pin_0, R5.Pin_0, R6.Pin_0, R7.Pin_0, R8.Pin_0, Part3.VCC, R12.Pin_0, R13.Pin_0
  GND: Mod1.GND, RW.E, RW.K, LW.E, LW.K, RB.E, RB.K, LWall.E, LWall.K, LDrop.E, LDrop.K, FDrop.E, FDrop.K, RDrop.E, RDrop.K, IR1.GND, IR2.GND, Motores.GND, Turbina.GND, Turbina.BIN2, Part3.GND, M1.Pin_4, Escovas.GND, Escovas.AIN1, LB.E, LB.K
  N12: Mod1.pin_20, M1.Pin_3, Escovas.PWRIN
  N13: Mod1.pin_21, Mod1.pin_22
  N14: Mod1.pin_27, Part3.SCL
  N15: Mod1.pin_28, LDrop.C
  N16: Mod1.pin_29, FDrop.C
  N17: Mod1.pin_30, RDrop.C
  N18: Mod1.pin_33, LB.C
  N19: Mod1.pin_34, RB.C
  N20: Mod1.pin_35, IR1.Data
  N21: Mod1.pin_36, LWall.C
  N22: RW.A, R5.Pin_1
  N23: LW.A, R4.Pin_1
  N24: RB.A, R3.Pin_1
  N25: LWall.A, R1.Pin_1
  N26: LDrop.A, R6.Pin_1
  N27: FDrop.A, R7.Pin_1
  N28: RDrop.A, R8.Pin_1
  N29: IR1.Vs, R12.Pin_1
  N30: IR2.Vs, R13.Pin_1
  N31: R2.Pin_1, LB.A
  N32: Motores.PWRIN, Turbina.PWRIN, M1.Pin_1

custom parts:
  Adafruit DRV8833 DC/Stepper Motor Driver: Spin two DC motors or step one bi-polar or uni-polar stepper with up to 1.2A per channel using the DRV8833. This motor driver chip is a nice alternative to the TB6612 driver. Like that chip, you get 2 full H-bridges, but this chip is better for low voltage uses (can run from 2.7V up to 10.8V motor power) and has built in current limiting capability. We set it up for 1A current limiting so you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
